# Fritzing sketch Soldering Fan (saved by Fritzing 1.0.1rc)
breadboards: 1

parts:
  V1 = DC Power [voltage=12V]
  U1 = Voltage Regulator [package=to220-adj]
  F1 = Fan - 4 wire [package=THT]
  R1 = Resistor [tolerance=±5% power=0.25W resistance=220 package=THT]
  1k = POT [knob_status=50% power=0.5W package=pot_mammoth]  # not connected
  1n4007 = Diode [package=diode-1n4001]
  D1 = Schottky Diode [part_number=1N4148 breakdown_voltage=3.6V package="300 mil [THT]"]
  D2 = Schottky Diode [part_number=1N4148 breakdown_voltage=3.6V package="300 mil [THT]"]
  U2 = POT [knob_status=50% power=0.5W package=pot_mammoth]
  U3 = 555 Timer [package="SO8 [SMD]"]
  R2 = Resistor [tolerance=±5% power=0.25W resistance=1k package=THT]
  F2 = Fan - 4 wire [package=THT]
  V3 = DC Power [voltage=24]
  C1 = Ceramic Capacitor [capacitance="100 nF" voltage=35V package="0603 [SMD, multilayer]"]
  U4 = Voltage Regulator [package=to220-igo]
  R3 = Resistor [tolerance=±5% power=0.25W resistance=4.7k package=THT]
  R4 = TRIMPOT [maximum_resistance=200kΩ knob_status=50% power=0.5W package=3386u]
  LED1 = LED - 3mm [color="Green (560nm)" current=0.030A package="3 mm [THT]"]
  S1 = Taiway 100-SP-X-T1 SPDT Miniature Toggle Switch [part_number=100-SP-X-T1-0-0-B1-M1 package=THT]

nets:
  N1: V1.V+, U1.IN
  N2: V1.V-, F1.GND
  N3: U1.ADJ, R1.Pin_0
  N4: U1.OUT, F1.Power, R1.Pin_1, 1n4007.C
  N5: D1.anode, U2.E
  N6: D2.cathode, U3.Pin_2, U3.Pin_6, C1.1
  N7: D2.anode, U2.A
  N8: U2.S, U3.Pin_3, F2.PWM
  GND: U3.Pin_1, F2.GND, V3.V-, U4.GND, LED1.cathode
  N9: U3.Pin_4, U3.Pin_8, R2.Pin_0, U4.OUT
  N10: U3.Pin_7, R2.Pin_1
  N11: F2.Power, U4.IN, S1.L1
  N12: V3.V+, S1.COM
  N13: R3.Pin_1, R4.CCW
  N14: R4.CW, LED1.anode

notes:
  Ensure that the PWM doesn't exceed 5V as it otherwise will be damaged
  The voltage regulator was not used. PWM is used
  https://circuitdigest.com/fullimage?i=circuitdiagram/PWM-generation-using-555-timer-IC-circuit-diagram.png

custom parts:
  Fan - 4 wire: Fan, 4 wire with tach.
